# Fritzing sketch MIcrobit and Ky-009 (saved by Fritzing 0.9.3b)

parts:
  R1 = BBC MicroBit
  R2 = Resistor [tolerance=±5% resistance=100 package=THT]
  R3 = Resistor [tolerance=±5% resistance=100 package=THT]
  Part1 = KY-009 Full Color RGB LED SMD Module [package="Breakout board"]
  R4 = Resistor [tolerance=±5% resistance=150 package=THT]

nets:
  N1: R1.GND, Part1.-
  N2: R1.P2_-_ANALOG_IN, R2.Pin_0
  N3: R1.P1_ANALOG_IN, R3.Pin_0
  N4: R1.P0_ANALOG_IN, R4.Pin_0
  N5: R2.Pin_1, Part1.G
  N6: R3.Pin_1, Part1.R
  N7: Part1.B, R4.Pin_1

custom parts:
  BBC MicroBit: The BBC MICRO:BIT
  KY-009 Full Color RGB LED SMD Module: RGB full color LED Module KY-009 for Arduino, emits a range of colors by mixing red, green and blue. The amount of each primary color is adjusted using PWM.
