# Fritzing sketch MIcrobit and Ky-011 (saved by Fritzing 0.9.3b)

parts:
  R1 = BBC MicroBit
  Part3 = KY-011 Two Color LED Module [package="Breakout board"]
  R2 = Resistor [tolerance=±5% resistance=100 package=THT]
  R3 = Resistor [tolerance=±5% resistance=100 package=THT]

nets:
  N1: R1.GND, Part3.-
  N2: R1.P2_-_ANALOG_IN, R3.Pin_0
  N3: R1.P1_ANALOG_IN, R2.Pin_0
  N4: Part3.S, R2.Pin_1
  N5: Part3.Vin, R3.Pin_1

custom parts:
  BBC MicroBit: The BBC MICRO:BIT
  KY-011 Two Color LED Module: KEYES KY-011 Two Color LED Module consist of a common cathode 3mm red/green LED.
