# Fritzing sketch MIcrobit and Ky-018 (saved by Fritzing 0.9.3b)

parts:
  R1 = BBC MicroBit
  Part1 = KY-018 Photoresistor Module [package="Breakout board"]

nets:
  N1: R1.GND, Part1.-
  3V3: R1.3v3, Part1.Vin
  N2: R1.P0_ANALOG_IN, Part1.S

custom parts:
  BBC MicroBit: The BBC MICRO:BIT
  KY-018 Photoresistor Module: KY-018 Photoresistor module, used to measure light intensity. It can determine the presence or absence of light.
