# Fritzing sketch MIcrobit and Ky-020 (saved by Fritzing 0.9.3b)

parts:
  Part2 = KY-020 Tilt Switch Module [package="Breakout board"]
  R1 = BBC MicroBit

nets:
  N1: Part2.S, R1.P1_ANALOG_IN
  VIN: Part2.Vin, R1.3v3
  N2: Part2.-, R1.GND

custom parts:
  KY-020 Tilt Switch Module: KY-020 Arduino tilt switch sensor module. Closes the circuit when it is tilted to the side as long as it is moved with enough force and degree of inclination to activate the ball switch inside.
  BBC MicroBit: The BBC MICRO:BIT
