# Fritzing sketch MIcrobit and Ky-021 (saved by Fritzing 0.9.3b)

parts:
  R1 = BBC MicroBit
  Part2 = KY-021 Mini Magnetic Reed Switch Module [package="Breakout board"]

nets:
  N1: R1.GND, Part2.-
  3V3: R1.3v3, Part2.Vin
  N2: R1.P0_ANALOG_IN, Part2.S

custom parts:
  BBC MicroBit: The BBC MICRO:BIT
  KY-021 Mini Magnetic Reed Switch Module: KY-021 magnetic reed switch module. A reed switch is a magnetic sensor that is normally open and gets closed when exposed to a magnetic field.
