# Fritzing sketch MIcrobit and Ky-031 (saved by Fritzing 0.9.3b)

parts:
  R1 = BBC MicroBit
  Mod1 = KY-031 Knock Sensor Module [package="Breakout board"]

nets:
  N1: R1.GND, Mod1.-
  3V3: R1.3v3, Mod1.Vin
  N2: R1.P0_ANALOG_IN, Mod1.S

custom parts:
  BBC MicroBit: The BBC MICRO:BIT
  KY-031 Knock Sensor Module: KY-031 Knock Sensor module. A vibration sensor that sends a signal when a knock/tap is detected.
