# Fritzing sketch MIcrobit and Ky-034 (saved by Fritzing 0.9.3b)

parts:
  R1 = BBC MicroBit
  Mod1 = KY-034 Automatic Flashing Color LED [package="Breakout board"]

nets:
  N1: R1.GND, Mod1.-
  N2: R1.P0_ANALOG_IN, Mod1.S

custom parts:
  BBC MicroBit: The BBC MICRO:BIT
  KY-034 Automatic Flashing Color LED: KY-034 Automatic Flashiing Color LED. A 7 color LED that flashes through a sequence of colors, creating a multicolored pattern of flashing light.
