# Fritzing sketch microbit and CCS811 (saved by Fritzing 0.9.3b)

parts:
  R1 = BBC MicroBit
  Part1 = Adafruit CCS811

nets:
  GND: R1.GND, Part1.GND
  N1: R1.P20_(SDA), Part1.SDA
  N2: R1.P19_(SCL), Part1.SCL
  3V3: R1.3v3, Part1.3.3V

custom parts:
  BBC MicroBit: The BBC MICRO:BIT
