# Fritzing sketch microbit and GUVA-S12SD (saved by Fritzing 0.9.3b)

parts:
  R1 = BBC MicroBit
  Part1 = GUVA-S12SD UV Light Sensor

nets:
  GND: R1.GND, Part1.GND
  3V3: R1.3v3, Part1.5V
  N1: R1.P0_ANALOG_IN, Part1.Out

custom parts:
  BBC MicroBit: The BBC MICRO:BIT
  GUVA-S12SD UV Light Sensor: Extend your light-sensing spectrum with this analog UV sensor module. It uses a UV photodiode, which can detect the 240-370nm range of light (which covers UVB and most of UVA spectrum). The signal level from the photodiode is very small, in the nano-ampere level, so we tossed on an opamp to amplify the signal to a more manageable volt-level.
