# Fritzing sketch microbit and MAG3110 (saved by Fritzing 0.9.3b)

parts:
  Part5 = MAG3110
  R1 = BBC MicroBit

nets:
  GND: Part5.GND, R1.GND
  VCC: Part5.VCC, R1.3v3
  N1: Part5.SDA, R1.P20_(SDA)
  N2: Part5.SCL, R1.P19_(SCL)

custom parts:
  MAG3110: Sparkfun MAG3110 Breakout
  BBC MicroBit: The BBC MICRO:BIT
