# Fritzing sketch microbit and MPL3115A2 (saved by Fritzing 0.9.3b)

parts:
  R1 = BBC MicroBit
  Part3 = MPL3115A2 I2C Barometric Pressure, Altitude, Temperature Sensor

nets:
  GND: R1.GND, Part3.GND
  N1: R1.P20_(SDA), Part3.SDA
  N2: R1.P19_(SCL), Part3.SCL
  3V3: R1.3v3, Part3.+3V3

custom parts:
  BBC MicroBit: The BBC MICRO:BIT
  MPL3115A2 I2C Barometric Pressure, Altitude, Temperature Sensor: This pressure sensor from Freescale is a great low-cost sensing solution for precision measurement of barometric pressure and altitude. The MPL3115A2 has a typical 1.5 Pascal resolution, which can resolve altitude at 0.3 meters (compare to the BMP180 which can do 0.17m). It has some upsides compared to the BMP180, such as interrupt outputs for ultra-low power usage, and its also a heck of a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
