# Fritzing sketch microbit and SI7021 (saved by Fritzing 0.9.3b)

parts:
  R1 = BBC MicroBit
  Part2 = Adafruit Si7021 Temp Humidity [part_number="Adafruit #3251"]

nets:
  GND: R1.GND, Part2.GND
  N1: R1.P20_(SDA), Part2.SDA
  N2: R1.P19_(SCL), Part2.SCL
  3V3: R1.3v3, Part2.+3V3

custom parts:
  BBC MicroBit: The BBC MICRO:BIT
  Adafruit Si7021 Temp Humidity: It's summer and you're sweating and your hair's all frizzy and all you really want to know is why the weatherman said this morning that today's relative humidity would max out at a perfectly reasonable 42% when it feels more like 77%. Enter the Si7021 Temperature + Humidity Sensor - the best way to prove the weatherman wrong! This lovely sensor for Silicon labs has ± 3% relative humidity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
