# Fritzing sketch microbit and TCS34725 (saved by Fritzing 0.9.3b)

parts:
  R1 = BBC MicroBit
  Part1 = Adafruit TCS34725 RGB Color Sensor [part_number="Adafruit #1334"]

nets:
  GND: R1.GND, Part1.GND
  N1: R1.P20_(SDA), Part1.SDA
  N2: R1.P19_(SCL), Part1.SCL
  3V3: R1.3v3, Part1.+3V3

custom parts:
  BBC MicroBit: The BBC MICRO:BIT
  Adafruit TCS34725 RGB Color Sensor: Your electronics can now see in dazzling color with this lovely color light sensor. We found the best color sensor on the market, the TCS34725, which has RGB and Clear light sensing elements. An IR blocking filter, integrated on-chip and localized to the color sensing photodiodes, minimizes the IR spectral component of the incoming light and allows color measurements to be made accurately. The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
