# Fritzing sketch microbit and TEMT6000 (saved by Fritzing 0.9.3b)

parts:
  R1 = BBC MicroBit
  Part1 = Ambient Light Sensor (TEMT6000 Breakout Board)

nets:
  GND: R1.GND, Part1.GND
  3V3: R1.3v3, Part1.VCC
  N1: R1.P1_ANALOG_IN, Part1.S

custom parts:
  BBC MicroBit: The BBC MICRO:BIT
