# Fritzing sketch microbit and TM1637 (saved by Fritzing 0.9.3b)

parts:
  R1 = BBC MicroBit
  Grove1 = Grove 4 Digit Display

nets:
  GND: R1.GND, Grove1.GND
  3V3: R1.3v3, Grove1.VCC
  N1: R1.P4_ANALOG_IN, Grove1.DIO
  N2: R1.P3_ANALOG_IN, Grove1.CLK

custom parts:
  BBC MicroBit: The BBC MICRO:BIT
