# Fritzing sketch microbit and VEML6070 (saved by Fritzing 0.9.3b)

parts:
  R1 = BBC MicroBit
  Part1 = VEML6070 [part_number=VEML6070]

nets:
  GND: R1.GND, Part1.GND
  N1: R1.P20_(SDA), Part1.SDA
  N2: R1.P19_(SCL), Part1.SCL
  3V3: R1.3v3, Part1.VDD

custom parts:
  BBC MicroBit: The BBC MICRO:BIT
  VEML6070: This little sensor is a great way to add UV light sensing to any microcontroller project. The VEML6070 from Vishay has a true UV A light sensor and an I2C-controlled ADC that will take readings and integrate them for you over ~60ms to 500ms.
