# Fritzing sketch microbit and VL53L0X (saved by Fritzing 0.9.3b)

parts:
  R1 = BBC MicroBit
  Part2 = Adafruit VL53L0X Time of Flight Distance Sensor [part_number="Adafruit #3317"]

nets:
  GND: R1.GND, Part2.GND
  N1: R1.P20_(SDA), Part2.SDA
  N2: R1.P19_(SCL), Part2.SCL
  3V3: R1.3v3, Part2.VIN

custom parts:
  BBC MicroBit: The BBC MICRO:BIT
  Adafruit VL53L0X Time of Flight Distance Sensor: The VL53L0X is a Time of Flight distance sensor like no other you've used! The sensor contains a very tiny invisible laser source, and a matching sensor. The VL53L0X can detect the "time of flight", or how long the light has taken to bounce back to the sensor. Since it uses a very narrow light source, it is good for determining distance of only the surface directly in front of it. Unlike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
