# Fritzing sketch microbit and ads1115 (saved by Fritzing 0.9.3b)

parts:
  R1 = BBC MicroBit
  Part1 = Adafruit ADS1115 16Bit I2C ADC [part_number="Adafruit #1085"]

nets:
  GND: R1.GND, Part1.GND
  N1: R1.P20_(SDA), Part1.SDA
  N2: R1.P19_(SCL), Part1.SCL
  3V3: R1.3v3, Part1.VDD

custom parts:
  BBC MicroBit: The BBC MICRO:BIT
  Adafruit ADS1115 16Bit I2C ADC: For microcontrollers without an analog-to-digital converter or when you want a higher-precision ADC, the ADS1115 provides 16-bit precision at 860 samples/second over I2C. The chip can be configured as 4 single-ended input channels, or two differential channels. As a nice bonus, it even includes a programmable gain amplifier, up to x16, to help boost up smaller single/differential signals to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
