# Fritzing sketch microbit and dht12 (saved by Fritzing 0.9.3b)

parts:
  R1 = BBC MicroBit
  DHT1 = DHT12 Humitidy and Temperature Sensor I2C.

nets:
  GND: R1.GND, DHT1.GND
  N1: R1.P20_(SDA), DHT1.SDA
  N2: R1.P19_(SCL), DHT1.SCL
  3V3: R1.3v3, DHT1.VDD

custom parts:
  BBC MicroBit: The BBC MICRO:BIT
  DHT12 Humitidy and Temperature Sensor I2C.: DHT12 Humidity and Temperature Sensor I2C. Supply voltage: 2.7V to 5.5V Current: Standby 30uA, Active 800uA Temperature: -20ºC to 60ºC, res. 0.1ºC Humidity: 20%RH to 95%RH, res. 0.1%RH ID I2C 0x5c
