# Fritzing sketch microbit and hmc588 (saved by Fritzing 0.9.3b)

parts:
  R1 = BBC MicroBit
  Part2 = Triple Axis Magnetometer - HMC5883 Breakout

nets:
  GND: R1.GND, Part2.GND
  N1: R1.P20_(SDA), Part2.SDA
  N2: R1.P19_(SCL), Part2.SCL
  3V3: R1.3v3, Part2.VCC

custom parts:
  BBC MicroBit: The BBC MICRO:BIT
