# Fritzing sketch microbit and mcp4725 (saved by Fritzing 0.9.3b)

parts:
  Part1 = Adafruit MCP4725 Breakout Board - 12-Bit DAC [part_number="Adafruit #935"]
  R1 = BBC MicroBit

nets:
  VDD: Part1.VDD, R1.3v3
  GND: Part1.GND, R1.GND
  N1: Part1.SCL, R1.P19_(SCL)
  N2: Part1.SDA, R1.P20_(SDA)
  N3: Part1.VOUT, R1.P0_ANALOG_IN

custom parts:
  Adafruit MCP4725 Breakout Board - 12-Bit DAC: Your microcontroller probably has an ADC (analog -> digital converter) but does it have a DAC (digital -> analog converter)??? Now it can! This breakout board features the easy-to-use MCP4725 12-bit DAC. Control it via I2C and send it the value you want it to output, and the VOUT pin will have it. Great for audio / analog projects, such as when you can't use PWM but need a sine wave or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
  BBC MicroBit: The BBC MICRO:BIT
