# Fritzing sketch microbit and mma7361 (saved by Fritzing 0.9.3b)

parts:
  U2 = MMA7361 [package=lga14]
  R1 = BBC MicroBit

nets:
  N1: U2.XOUT, R1.P0_ANALOG_IN
  N2: U2.YOUT, R1.P1_ANALOG_IN
  N3: U2.ZOUT, R1.P2_-_ANALOG_IN
  VSS: U2.VSS, R1.3v3
  N4: U2.G, R1.GND

custom parts:
  MMA7361: 3-axis 1.5/6g analog output accelerometer
  BBC MicroBit: The BBC MICRO:BIT
