# Fritzing sketch microbit and oled (saved by Fritzing 0.9.3b)

parts:
  R1 = BBC MicroBit
  Part1 = OLED Monochrome 128x32 I2C [part_number=931]

nets:
  GND: R1.GND, Part1.GND
  N1: R1.P20_(SDA), Part1.SDA
  N2: R1.P19_(SCL), Part1.SCL
  3V3: R1.3v3, Part1.3.3V

custom parts:
  BBC MicroBit: The BBC MICRO:BIT
  OLED Monochrome 128x32 I2C: These displays are small, only about 1" diagonal, but very readable due to the high contrast of an OLED display. This display is made of 128x32 individual white OLED pixels, each one is turned on or off by the controller chip. Because the display makes its own light, no backlight is required. This reduces the power required to run the OLED and is why the display has such high contrast; we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
