# Fritzing sketch microbit and sht11 (saved by Fritzing 0.9.3b)

parts:
  R1 = BBC MicroBit
  Part1 = SHT1x-Breakout

nets:
  GND: R1.GND, Part1.GND
  3V3: R1.3v3, Part1.VCC
  N1: R1.P4_ANALOG_IN, Part1.SCK
  N2: R1.P3_ANALOG_IN, Part1.DATA

custom parts:
  BBC MicroBit: The BBC MICRO:BIT
