# Fritzing sketch microbit and traffic light (saved by Fritzing 0.9.3b)
breadboards: 1

parts:
  R1 = BBC MicroBit
  R2 = Resistor [tolerance=±5% resistance=470 package=THT]
  LED1 = LED - 5mm [color="Red (633nm)" package="5 mm [THT]"]
  LED2 = LED - 5mm [color="Yellow (595nm)" package="5 mm [THT]"]
  R3 = Resistor [tolerance=±5% resistance=470 package=THT]
  R4 = Resistor [tolerance=±5% resistance=470 package=THT]
  LED3 = LED - 5mm [color="Green (570nm)" package="5 mm [THT]"]

nets:
  N1: R1.GND, LED1.cathode, LED2.cathode, LED3.cathode
  N2: R1.P2_-_ANALOG_IN, R2.Pin_0
  N3: R1.P1_ANALOG_IN, R3.Pin_0
  N4: R1.P7, R1.P5_BUTTON_A
  N5: R1.P0_ANALOG_IN, R4.Pin_0
  N6: R2.Pin_1, LED3.anode
  N7: LED1.anode, R4.Pin_1
  N8: LED2.anode, R3.Pin_1

custom parts:
  BBC MicroBit: The BBC MICRO:BIT
